// Digital circuit Lab_01_AND.dig as structural Verilog
module Lab_01_AND (
  input  X,
  input  Y,
  input  Z,
  output Output
);

  wire and_1_out, and_2_out, and_3_out, and_4_out, not_1_out, not_2_out, not_3_out, not_4_out, not_5_out,
       not_6_out;

  not not_1 (not_1_out, X);
  not not_2 (not_2_out, Y);
  not not_3 (not_3_out, Z);
  and and_1 (and_1_out, not_1_out, not_2_out);
  and and_2 (and_2_out, not_1_out, Y, not_3_out);
  and and_3 (and_3_out, X, not_2_out, not_3_out);
  not not_4 (not_4_out, and_1_out);
  not not_5 (not_5_out, and_2_out);
  not not_6 (not_6_out, and_3_out);
  and and_4 (and_4_out, not_4_out, not_5_out, not_6_out);
  not not_7 (Output, and_4_out);
  LED led_1 (.in(Output));
endmodule
