// Digital circuit 4_bit_adder.dig as structural Verilog
module _4_bit_adder (
  input  a0,
  input  a1,
  input  a2,
  input  a3,
  input  b0,
  input  b1,
  input  b2,
  input  b3,
  input  _0,
  output T0,
  output T1,
  output T2,
  output T3,
  output E3
);

  wire full_adder_1_e, full_adder_2_e, full_adder_3_e;

  full_adder full_adder_1 (.Eg(_0), .a(a0), .b(b0), .T(T0), .E(full_adder_1_e));
  full_adder full_adder_2 (.Eg(full_adder_1_e), .a(a1), .b(b1), .T(T1), .E(full_adder_2_e));
  full_adder full_adder_3 (.Eg(full_adder_2_e), .a(a2), .b(b2), .T(T2), .E(full_adder_3_e));
  full_adder full_adder_4 (.Eg(full_adder_3_e), .a(a3), .b(b3), .T(T3), .E(E3));

  // Notes on the sheet:
  //   4 Bit Toplayıcı
endmodule
