// Digital circuit 4_bit_subtractor.dig as structural Verilog
module _4_bit_subtractor (
  input  a0,
  input  a1,
  input  a2,
  input  a3,
  input  b0,
  input  b1,
  input  b2,
  input  b3,
  input  _0,
  output F0,
  output F1,
  output F2,
  output F3,
  output B3_2
);

  wire full_subtractor_1_b, full_subtractor_2_b, full_subtractor_3_b;

  full_subtractor full_subtractor_1 (.Bg(_0), .a(a0), .b_2(b0), .F(F0), .B(full_subtractor_1_b));
  full_subtractor full_subtractor_2 (.Bg(full_subtractor_1_b), .a(a1), .b_2(b1), .F(F1), .B(full_subtractor_2_b));
  full_subtractor full_subtractor_3 (.Bg(full_subtractor_2_b), .a(a2), .b_2(b2), .F(F2), .B(full_subtractor_3_b));
  full_subtractor full_subtractor_4 (.Bg(full_subtractor_3_b), .a(a3), .b_2(b3), .F(F3), .B(B3_2));

  // Notes on the sheet:
  //   4 Bit Çıkarıcı
endmodule
