// Digital circuit full_adder.dig as structural Verilog
module full_adder (
  input  Eg,
  input  a,
  input  b,
  output T,
  output E
);

  wire and_1_out, and_2_out, or_1_out;

  xor xor_1 (T, Eg, a, b);
  and and_1 (and_1_out, a, b);
  or or_1 (or_1_out, a, b);
  and and_2 (and_2_out, or_1_out, Eg);
  or or_2 (E, and_1_out, and_2_out);

  // Notes on the sheet:
  //   Tam Toplayıcı
endmodule
