// Digital circuit full_adder_with_half_adders.dig as structural Verilog
module full_adder_with_half_adders (
  input  Eg,
  input  a,
  input  b,
  output T,
  output E
);

  wire half_adder_1_e, half_adder_1_t, half_adder_2_e;

  half_adder half_adder_1 (.a(a), .b(b), .T(half_adder_1_t), .E(half_adder_1_e));
  half_adder half_adder_2 (.a(Eg), .b(half_adder_1_t), .T(T), .E(half_adder_2_e));
  or or_1 (E, half_adder_2_e, half_adder_1_e);

  // Notes on the sheet:
  //   Tam Toplayıcı
endmodule
