// Digital circuit full_subtractor.dig as structural Verilog
module full_subtractor (
  input  Bg,
  input  a,
  input  b_2,
  output F,
  output B
);

  wire and_1_out, and_2_out, and_3_out, not_1_out, not_2_out;

  not not_1 (not_1_out, a);
  not not_2 (not_2_out, a);
  xor xor_1 (F, a, b_2, Bg);
  and and_1 (and_1_out, not_1_out, b_2);
  and and_2 (and_2_out, not_2_out, Bg);
  and and_3 (and_3_out, b_2, Bg);
  or or_1 (B, and_1_out, and_2_out, and_3_out);

  // Notes on the sheet:
  //   Tam Çıkarıcı
endmodule
