// Digital circuit half_adder.dig as structural Verilog
module half_adder (
  input  a,
  input  b,
  output T,
  output E
);

  xor xor_1 (T, a, b);
  and and_1 (E, a, b);

  // Notes on the sheet:
  //   Yarı Toplayıcı
endmodule
