// Digital circuit half_subtractor.dig as structural Verilog
module half_subtractor (
  input  a,
  input  b,
  output F,
  output B_2
);

  wire not_1_out;

  not not_1 (not_1_out, a);
  xor xor_1 (F, a, b);
  and and_1 (B_2, not_1_out, b);
endmodule
