// Digital circuit Lab_01_OR.dig as structural Verilog
module Lab_01_OR (
  input  X,
  input  Y,
  input  Z,
  output F_X__Y__Z
);

  wire not_1_out, not_2_out, not_3_out, not_4_out, not_5_out, not_6_out, not_7_out, or_1_out, or_2_out,
       or_3_out, or_4_out;

  not not_1 (not_1_out, X);
  not not_2 (not_2_out, Y);
  not not_3 (not_3_out, Z);
  or or_1 (or_1_out, X, Y, Z);
  or or_2 (or_2_out, X, Y, not_3_out);
  or or_3 (or_3_out, X, not_2_out, Z);
  or or_4 (or_4_out, not_1_out, Y, Z);
  not not_4 (not_4_out, or_1_out);
  not not_5 (not_5_out, or_2_out);
  not not_6 (not_6_out, or_3_out);
  not not_7 (not_7_out, or_4_out);
  or or_5 (F_X__Y__Z, not_4_out, not_5_out, not_6_out, not_7_out);
  LED led_1 (.in(F_X__Y__Z));
endmodule
