// Digital circuit Lab_02.dig as structural Verilog
module Lab_02 (
  input  X,
  input  Y,
  input  Z,
  input  W,
  output Output
);

  wire and_1_out, and_2_out, not_1_out, not_2_out, not_3_out, not_4_out;

  not not_1 (not_1_out, X);
  not not_2 (not_2_out, Y);
  not not_3 (not_3_out, Z);
  not not_4 (not_4_out, W);
  and and_1 (and_1_out, not_1_out, Z, not_4_out);
  and and_2 (and_2_out, X, Y);
  or or_1 (Output, W, and_1_out, and_2_out);
  LED led_1 (.in(Output));
endmodule
