// Digital circuit Lab_03.dig as structural Verilog
module Lab_03 (
  input  A,
  input  B,
  input  C,
  input  D,
  output F
);

  wire not_1_out;

  not not_1 (not_1_out, A);
  Multiplexer #(.Selector_Bits(3)) multiplexer_1 (
    .sel({B, C, D}), .in_0(1'b1), .in_1(A), .in_2(A), .in_3(A), .in_4(1'b1), .in_5(not_1_out), .in_6(1'b0),
    .in_7(not_1_out), .out(F));
endmodule
