// Digital circuit Lab_04.dig as structural Verilog
module Lab_04 (
  input  clk,
  input  X,
  output Z
);

  wire and_1_out, and_2_out, and_3_out, and_4_out, and_5_out, and_6_out, and_7_out, and_9_out, not_1_out,
       or_1_out, or_2_out, or_3_out, or_4_out, Q0_nq, Q0_q, Q1_q, Q2_nq, Q2_q;

  not not_1 (not_1_out, X);
  and and_1 (and_1_out, Q0_q, Q1_q, not_1_out);
  or or_1 (or_1_out, Q0_q, X);
  and and_2 (and_2_out, not_1_out, Q1_q);
  JK_FF Q2 (.J(and_1_out), .C(clk), .K(or_1_out), .Q(Q2_q), .nQ(Q2_nq));
  or or_2 (or_2_out, and_2_out, and_3_out);
  and and_3 (and_3_out, Q0_q, Q1_q);
  and and_4 (and_4_out, Q2_q, X, Q0_nq);
  JK_FF Q1 (.J(or_3_out), .C(clk), .K(or_2_out), .Q(Q1_q));  // open: nQ
  or or_3 (or_3_out, and_4_out, and_5_out);
  and and_5 (and_5_out, Q2_nq, not_1_out, Q0_q);
  and and_6 (and_6_out, Q2_q, Q0_nq);
  JK_FF Q0 (.J(or_4_out), .C(clk), .K(and_9_out), .Q(Q0_q), .nQ(Q0_nq));
  or or_4 (or_4_out, and_6_out, and_7_out);
  and and_7 (and_7_out, Q2_nq, X);
  and and_8 (Z, Q2_q, Q0_q);
  and and_9 (and_9_out, Q0_q, not_1_out);
endmodule
